# Fritzing sketch schema_v2 (saved by Fritzing 0.8.2b)

parts:
  U1 = ESP8266 NodeMCU LoLin module
  S1 = H-Bridge with L298N
  M2 = DC Motor
  M3 = DC Motor
  U2 = SWITCH-SPST-2 [package=switch-spst-vertical]
  VCC1 = Battery
  M4 = DC Motor
  M5 = DC Motor

nets:
  N1: U1.D3, S1.IN4
  N2: U1.D4, S1.IN3
  GND: U1.GND, S1.GND, VCC1.-
  N3: U1.D5, S1.ENA
  N4: U1.D6, S1.ENB
  N5: U1.D7, S1.IN2
  N6: U1.D8, S1.IN1
  VIN: U1.Vin, S1.5V
  N7: S1.12V, U2.P
  N8: S1.M1-01, M4.pin_1, M5.pin_1
  N9: S1.M1-02, M4.pin_2, M5.pin_2
  N10: S1.M2-01, M2.pin_2, M3.pin_2
  N11: S1.M2-02, M2.pin_1, M3.pin_1
  N12: U2.O, VCC1.+

custom parts:
  ESP8266 NodeMCU LoLin module: ESP8266 based NodeMCU
  H-Bridge with L298N: h-bridge
